# Fritzing sketch schema_fritzing (saved by Fritzing 0.9.3b)
breadboards: 1

parts:
  U1 = ESP8266 WiFi Module [part_number=ESP8266]
  U2 = RELAY [package=relay-g5q]
  U4 = V_REG_LD1117VXX [package=78xxl]
  C3 = Electrolytic Capacitor [capacitance=1µF package="100 mil [THT, electrolytic]"]
  C4 = Electrolytic Capacitor [capacitance=1µF package="100 mil [THT, electrolytic]"]
  R1 = Resistor [tolerance=±5% resistance=220 package=THT]
  S1 = Pushbutton [package="[THT]"]
  R2 = Resistor [tolerance=±5% resistance=220 package=THT]
  Q1 = NPN-Transistor [package="TO92 [THT]"]
  D1 = Rectifier Diode [part_number=1N4001 package="300 mil [THT]"]

nets:
  3.3V: U1.VCC, U1.CH_PD, U4.OUT, C3.+, R1.Pin_1, R2.Pin_0
  N1: U1.GPIO_0, R1.Pin_0, S1.Pin_3, S1.Pin_4
  N2: U1.GPIO_2, R2.Pin_1, Q1.B
  GND: U1.GND, U4.GND, C3.-, C4.-, S1.Pin_1, Q1.E
  N3: U2.COIL2, Q1.C, D1.anode
  5V: U2.COIL1, U4.IN, C4.+, D1.cathode

custom parts:
  ESP8266 WiFi Module: Generic WiFi Module based on the ESP8266 with onboard PCB antenna and UART communications
